# Fritzing sketch hyperpan (saved by Fritzing 0.9.2b)

parts:
  Part1 = Adafruit Perma-Proto HAT [part_number="Adafruit #2314 and #2310"]
  R1 = Resistor [tolerance=±5% resistance=330 package="0603 [SMD]"]
  Alerts = smd LED [color="Red (633nm)" package="1206 [SMD]"]  # not connected
  U1 = TLP621 [package=THT]
  U2 = TLP621 [package=THT]
  R2 = Resistor [tolerance=±5% resistance=330 package="0603 [SMD]"]
  R3 = Resistor [tolerance=±5% resistance=330 package="0603 [SMD]"]
  Focus = smd LED [color="Green (560nm)" package="1206 [SMD]"]
  Shutter = smd LED [color="Red (633nm)" package="1206 [SMD]"]

nets:
  N1: Part1.GPIO4, U1.Pin_1
  N2: Part1.GPIO17, U2.Pin_1
  N3: Part1.GND, R1.Pin_1, R2.Pin_1, R3.Pin_1
  N4: U1.Pin_2, Focus.anode
  N5: U2.Pin_2, Shutter.anode

custom parts:
  Adafruit Perma-Proto HAT: To kick off the Adafruit HAT party, we have this Perma-Proto inspired plug in daughter board. It has a grid of 0.1" prototyping soldering holes for attaching chips, resistors, LED, potentiometers and more. The holes are connected underneath with traces to mimic the solderless breadboards you're familiar. There's also long power strips for +3V, +5V and Ground connections to the Pi. Near the top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
